// Logisim project amra_mustajbasic_20117.circ as structural Verilog: 9 circuits, main circuit main
module main (
  input  in_1,
  input  in_2
);

  wire clock_1_out, comp_1_o, maincontrol_1_alusrc, maincontrol_1_beq, maincontrol_1_bne,
       maincontrol_1_extop, maincontrol_1_j, maincontrol_1_memread, maincontrol_1_memtoreg,
       maincontrol_1_memwrite, maincontrol_1_regdest, nextpc_1_pcsrc, registerfile_1_p3, registerfile_1_p7;
  wire [1:0] incrementer_1_p3;
  wire [3:0] mips_alu_1_p3;
  wire [4:0] mipsprogramrom_1_p2_2, multiplexer_2_out;
  wire [25:0] mipsprogramrom_1_p3;
  wire [29:0] incrementer_1_p1, incrementer_1_p2, mipsprogramrom_1_p1, multiplexer_1_out;
  wire [31:0] extender_1_out_3, mips_alu_1_p5, mips_ram_1_p6, mipsprogramrom_1_p2, multiplexer_3_out,
       registerfile_1_p1, registerfile_1_p8;

  Multiplexer #(.width(30), .enable("false")) multiplexer_1 (
    .in0(incrementer_1_p2), .in1(incrementer_1_p2), .out(multiplexer_1_out), .sel(nextpc_1_pcsrc));
  Clock clock_1 (.out(clock_1_out));
  // Incrementer #(.width(30)) incrementer_1: pin names not known; wires that end beside it: incrementer_1_p1, incrementer_1_p2, {incrementer_1_p1, incrementer_1_p3}, incrementer_1_p2
  Register #(.width(32)) register_1 (
    .D({multiplexer_1_out, 2'b00}), .en(in_1), .clk(clock_1_out), .Q({incrementer_1_p1, incrementer_1_p3}),
    .clr(in_2));
  // MIPSProgramROM mipsprogramrom_1: pin names not known; wires that end beside it: mipsprogramrom_1_p1, {mipsprogramrom_1_p2[31:11], mipsprogramrom_1_p2_2, mipsprogramrom_1_p2[5:0]}, mipsprogramrom_1_p3
  Multiplexer #(.width(5), .enable("false")) multiplexer_2 (
    .in0(mipsprogramrom_1_p2[20:16]), .in1(mipsprogramrom_1_p2[15:11]), .out(multiplexer_2_out),
    .sel(maincontrol_1_regdest));
  // RegisterFile registerfile_1: pin names not known; wires that end beside it: registerfile_1_p1, clock_1_out, registerfile_1_p3, multiplexer_2_out, mipsprogramrom_1_p2[25:21], mipsprogramrom_1_p2[20:16], registerfile_1_p7, registerfile_1_p8
  extender extender_1 (
    .immediate({mipsprogramrom_1_p2[15:11], mipsprogramrom_1_p2_2, mipsprogramrom_1_p2[5:0]}),
    .extOp(maincontrol_1_extop), .out_3(extender_1_out_3));
  Multiplexer #(.width(32), .enable("false")) multiplexer_3 (
    .in0(registerfile_1_p8), .in1(extender_1_out_3), .out(multiplexer_3_out), .sel(maincontrol_1_alusrc));
  mainControl maincontrol_1 (
    .opcode(mipsprogramrom_1_p2[31:26]), .regDest(maincontrol_1_regdest), .regWrite(registerfile_1_p3),
    .extOp(maincontrol_1_extop), .aluSrc(maincontrol_1_alusrc), .beq(maincontrol_1_beq),
    .bne(maincontrol_1_bne), .j(maincontrol_1_j), .memRead(maincontrol_1_memread),
    .memWrite(maincontrol_1_memwrite), .memToReg(maincontrol_1_memtoreg));
  comp comp_1 (.in_1(mips_alu_1_p5), .O(comp_1_o));
  // Mips_ALU mips_alu_1: pin names not known; wires that end beside it: registerfile_1_p7, multiplexer_3_out, mips_alu_1_p3, mipsprogramrom_1_p2_2, mips_alu_1_p5
  NextPC nextpc_1 (
    .Add(incrementer_1_p2), .IncPC(mipsprogramrom_1_p1), .Beq(maincontrol_1_beq), .Bne(maincontrol_1_bne),
    .J(maincontrol_1_j), .Imm26(mipsprogramrom_1_p3), .Zero(comp_1_o), .PCSrc(nextpc_1_pcsrc));
  aluControl alucontrol_1 (
    .funct(mipsprogramrom_1_p2[5:0]), .opcode(mipsprogramrom_1_p2[31:26]), .out_3(mips_alu_1_p3));
  Multiplexer #(.width(32), .enable("false")) multiplexer_4 (
    .in0(mips_alu_1_p5), .in1(mips_ram_1_p6), .out(registerfile_1_p1), .sel(maincontrol_1_memtoreg));
  // MIPS_RAM #(.addrWidth(24)) mips_ram_1: pin names not known; wires that end beside it: mips_alu_1_p5[23:0], registerfile_1_p8, maincontrol_1_memwrite, clock_1_out, maincontrol_1_memread, mips_ram_1_p6

  // Notes on the sheet:
  //   contents of mipsprogramrom_1 (hex, n*v repeats v):
  //   addiu $t1,$0,0 addiu $t2,$0,6 addiu $t3,$0,8 ori $t4,$t2,32 andi $t5,$t1,20 xori $t6,$t1,52 sw
  //   $t3,0($0) sw $t4,2($0) sw $t5,4($0)  beq $t0,$t1,label  addiu $t0,$0,2 addiu $t1,$0,4   label:
  //   addiu $t0,$0,0 addiu $t1,$0,0 j end  end: addiu $t0,$0,10 addiu $t1,$0,20 lw $t0,0($0) lw $t1,2($0)
endmodule

module extender (
  input  [15:0] immediate,
  input  extOp,
  output [31:0] out_3
);

  and and_1 (out_3[31], immediate[15], extOp);

  assign out_3[30:0] = {{15{out_3[31]}}, immediate};
endmodule

module mainControl (
  input  [5:0] opcode,
  output regDest,
  output regWrite,
  output extOp,
  output aluSrc,
  output beq,
  output bne,
  output j,
  output memRead,
  output memWrite,
  output memToReg
);

  wire and_3_out, and_4_out, and_5_out, not_1_out, not_2_out, not_3_out, not_4_out, not_5_out, not_6_out,
       not_8_out, not_9_out, not_10_out, not_11_out, not_12_out, not_13_out, not_14_out;

  not not_1 (not_1_out, opcode[3]);
  not not_2 (not_2_out, opcode[1]);
  not not_3 (not_3_out, opcode[2]);
  not not_4 (not_4_out, opcode[1]);
  not not_5 (not_5_out, opcode[5]);
  not not_6 (not_6_out, opcode[3]);
  not not_7 (extOp, opcode[2]);
  or or_1 (aluSrc, opcode[1], opcode[3]);
  not not_8 (not_8_out, opcode[3]);
  not not_9 (not_9_out, opcode[0]);
  not not_10 (not_10_out, opcode[3]);
  not not_11 (not_11_out, opcode[1]);
  not not_12 (not_12_out, opcode[3]);
  not not_13 (not_13_out, opcode[0]);
  not not_14 (not_14_out, opcode[3]);
  and and_1 (memWrite, opcode[5], opcode[3]);
  and and_2 (regDest, not_1_out, not_2_out);
  and and_3 (and_3_out, not_3_out, not_4_out);
  and and_4 (and_4_out, not_5_out, opcode[3]);
  or or_2 (regWrite, and_3_out, and_4_out, and_5_out);
  and and_5 (and_5_out, opcode[5], not_6_out);
  and and_6 (beq, not_8_out, opcode[2], not_9_out);
  and and_7 (bne, not_10_out, not_11_out, opcode[0]);
  and and_8 (j, not_12_out, opcode[1], not_13_out);
  and and_9 (memRead, opcode[5], not_14_out);

  assign memToReg = opcode[5];
endmodule

module aluControl (
  input  [5:0] funct,
  input  [5:0] opcode,
  output [3:0] out_3
);

  wire nor_1_out;
  wire [3:0] aluitip_1_o3, alurtip_1_o3;

  aluRtip alurtip_1 (
    .f0(funct[5]), .f1(funct[4]), .f2(funct[3]), .f3(funct[2]), .f4(funct[1]), .f5(funct[0]),
    .o0(alurtip_1_o3[3]), .o1(alurtip_1_o3[2]), .o2(alurtip_1_o3[1]), .o3(alurtip_1_o3[0]));
  nor nor_1 (nor_1_out, opcode[5], opcode[4], opcode[3], opcode[2], opcode[1], opcode[0]);
  aluItip aluitip_1 (
    .op0(opcode[5]), .op1(opcode[4]), .op2(opcode[3]), .op3(opcode[2]), .op4(opcode[1]), .op5(opcode[0]),
    .o0(aluitip_1_o3[3]), .o1(aluitip_1_o3[2]), .o2(aluitip_1_o3[1]), .o3(aluitip_1_o3[0]));
  Multiplexer #(.width(4), .enable("false")) multiplexer_1 (
    .in0(aluitip_1_o3), .in1(alurtip_1_o3), .out(out_3), .sel(nor_1_out));
endmodule

module aluRtip (
  input  f0,
  input  f1,
  input  f2,
  input  f3,
  input  f4,
  input  f5,
  output o0,
  output o1,
  output o2,
  output o3
);

  wire and_2_out, and_3_out, not_1_out, not_2_out, not_3_out;

  and and_1 (o2, f0, f5);
  not not_1 (not_1_out, f0);
  not not_2 (not_2_out, f4);
  not not_3 (not_3_out, f5);
  and and_2 (and_2_out, not_1_out, f5);
  and and_3 (and_3_out, f0, not_2_out, not_3_out);
  or or_1 (o3, and_2_out, and_3_out);

  assign o0 = f3;
  assign o1 = f4;
endmodule

module aluItip (
  input  op0,
  input  op1,
  input  op2,
  input  op3,
  input  op4,
  input  op5,
  output o0,
  output o1,
  output o2,
  output o3
);

  wire and_2_out, and_3_out, not_1_out, not_2_out, not_3_out, not_4_out;

  and and_1 (o0, op2, op3);
  not not_1 (not_1_out, op2);
  not not_2 (not_2_out, op4);
  not not_3 (not_3_out, op5);
  not not_4 (not_4_out, op2);
  and and_2 (and_2_out, not_1_out, not_2_out);
  and and_3 (and_3_out, op4, not_3_out);
  or or_1 (o2, not_4_out, op5);
  or or_2 (o1, and_2_out, and_3_out);

  assign o3 = 1'b0;
endmodule

module extender30 (
  input  [15:0] imm16,
  input  [29:0] imm30
);

  and and_1 (imm30[29], imm16[15], 1'b1);

  assign imm30[28:0] = {{13{imm30[29]}}, imm16};
endmodule

module comp (
  input  [31:0] in_1,
  output O
);

  Comparator #(.width(32)) comparator_1 (.a(in_1), .b({32{1'b0}}), .eq(O));  // open: gt, lt
endmodule

module NextPC (
  input  [29:0] Add,
  input  [29:0] IncPC,
  input  Beq,
  input  Bne,
  input  J,
  input  [25:0] Imm26,
  input  Zero,
  output PCSrc
);

  wire and_1_out, and_2_out;
  wire [29:0] adder_1_out, undriven;

  extender30 extender30_1 (.imm16(Imm26[15:0]), .imm30(undriven));
  Adder #(.width(30)) adder_1 (.a(IncPC), .b(undriven), .out(adder_1_out));  // open: cin, cout
  Multiplexer #(.width(30), .enable("false")) multiplexer_1 (
    .in0(adder_1_out), .in1({IncPC[29:26], Imm26}), .out(Add), .sel(J));
  and and_1 (and_1_out, ~Zero, Bne);  // AND_Gate
  or or_1 (PCSrc, and_1_out, J, and_2_out);
  and and_2 (and_2_out, Zero, Beq);
endmodule
